# Fritzing sketch platine (saved by Fritzing 0.9.2b)
circuit board: 8.46667cm x 5.64444cm
stripboards: 1

parts:
  J1 = Piezo Speaker
  503_temp_sensor = Resistor [tolerance=±5% resistance=50k package=THT]
  Composant1 = Arduino Uno (Rev3)
  R1 = Resistor [tolerance=±5% resistance=220 package=THT]
  S1 = Round Pushbutton
  S2 = Round Pushbutton
  R3 = Resistor [tolerance=±5% resistance=220 package=THT]
  R4 = Resistor [tolerance=±5% resistance=220 package=THT]

nets:
  N1: J1.pin1, Composant1.GND, R1.Pin_0, R3.Pin_0, R4.Pin_0
  N2: J1.pin2, Composant1.D7
  N3: 503_temp_sensor.Pin_0, Composant1.A1, R1.Pin_1
  N4: 503_temp_sensor.Pin_1, Composant1.5V, S1.leg1, S2.leg1
  N5: Composant1.A2, S1.leg0, R4.Pin_1
  N6: Composant1.A3, S2.leg0, R3.Pin_1
