# Fritzing sketch platine_screwshield (saved by Fritzing 0.9.2b)

parts:
  J1 = Piezo Speaker
  Composant1 = Arduino Uno (Rev3)
  S1 = Round Pushbutton
  S2 = Round Pushbutton
  Composant2 = Arduino ProtoScrew Shield Kit
  R5 = Resistor [tolerance=±5% resistance=220 package=THT]
  Composant3 = DeuLigne 1.1 - The Snootlab's LCD shield for Arduino
  503_(50k) = Temperature Sensor (Thermistor) [thermistor_type=NTC package=THT]
  R6 = Resistor [tolerance=±5% resistance=220 package=THT]

nets:
  GND: J1.pin1, Composant1.GND, S1.leg0, S2.leg0, Composant2.GND, R5.Pin_1, R6.Pin_0
  N1: J1.pin2, Composant2.D10
  N2: Composant1.A0, Composant3.A0
  N3: Composant1.A1, Composant2.A1, R5.Pin_0
  N4: Composant1.A4/SDA, Composant3.A4(SDA)
  N5: Composant1.A5/SCL, Composant3.A5(CLK)
  5V: Composant1.5V, Composant2.5V, 503_(50k).pin_1
  N6: S1.leg1, Composant2.D12
  N7: S2.leg1, Composant2.D11
  N8: Composant2.A2, 503_(50k).pin_0, R6.Pin_1
