# Fritzing sketch shield_detect_arret_chaudiere (saved by Fritzing 0.9.2b)
stripboards: 1

parts:
  Composant1 = DeuLigne 1.1 - The Snootlab's LCD shield for Arduino  # not connected
  Composant2 = Arduino Uno (Rev3)  # not connected
  R1 = Resistor [tolerance=±5% resistance=220 package=THT]
  S1 = Pushbutton [package="[THT]"]
  R2 = Resistor [tolerance=±5% resistance=220 package=THT]

nets:
  vers R1: R1.Pin_0
  N1: R1.Pin_1, S1.Pin_3, S1.Pin_4
  N2: S1.Pin_1, S1.Pin_2, R2.Pin_0

notes:
  n'est pas représenté sur la platine :
  1. derniere colonne à droite à moitié coupée n'est pas représenté
  2. les deux colonnes a gauche sur la moitié de la hauteur
